# Fritzing sketch circuit (saved by Fritzing 0.9.2b)
breadboards: 1

parts:
  C2 = Ceramic Capacitor [capacitance=100nF package="100 mil [THT, multilayer]"]
  12V_input = Power plug
  R1 = Resistor [tolerance=±1% resistance=56k package=THT]
  R2 = Resistor [tolerance=±1% resistance=10k package=THT]
  R4 = Resistor [tolerance=±1% resistance=10k package=THT]
  R3 = Resistor [tolerance=±1% resistance=10k package=THT]
  U1 = NodeMCU V1.0
  R5 = Resistor [tolerance=±1% resistance=10k package=THT]
  IC2 = IC, DIP package, 14 pins [chip_label=LMC6484N]

nets:
  N1: C2.0, R1.Pin_1, IC2.pin9
  N2: C2.1, R4.Pin_0, IC2.pin8
  N3: 12V_input.GND, IC2.pin11
  N4: 12V_input.VCC, IC2.pin4
  N5: R1.Pin_0, U1.D7
  N6: R2.Pin_0, U1.Vin
  N7: R2.Pin_1, R3.Pin_1, IC2.pin10
  N8: R4.Pin_1, U1.A0, R5.Pin_1
  N9: R3.Pin_0, U1.GND, R5.Pin_0

custom parts:
  NodeMCU V1.0: ESP8266 based NodeMCU
